# Fritzing sketch circuit (saved by Fritzing 0.9.3b)
perfboards: 1

parts:
  R2 = Resistor [tolerance=±5% resistance=1k package=THT]
  C1 = Electrolytic Capacitor [capacitance=1000µF package="300 mil [THT, electrolytic]"]
  Composant1 = Arduino Pro Mini v13
  Raspberry_Pi_B_rev1 = Raspberry Pi B rev1
  Composant2 = Adafruit DS3231 [part_number="Adafruit #3013"]
  U4 = RELAY-2 [package=relay-g5v]
  Q1 = NPN-Transistor [package="TO92 [THT]"]
  Composant3 = TXB0108 8-channel Bi-directional Logic Level Converter
  Couvercle = Toggle Switch [package=THT]

nets:
  N1: R2.Pin_0, Composant1.D9_PWM
  N2: R2.Pin_1, Q1.B
  N3: C1.-, Q1.E
  5V: C1.+, Composant1.RAW, U4.6, U4.9
  VCC: Composant1.VCC, Composant2.Vin, Composant3.VCCA
  GND: Composant1.GND, Raspberry_Pi_B_rev1.GND, Composant2.GND, Composant3.GND, Couvercle.L1
  N4: Composant1.A4, Composant2.SDA, Composant3.A1
  N5: Composant1.A5, Composant2.SCL, Composant3.A2
  N6: Composant1.D11_PWM/MOSI, Composant3.A3
  N7: Composant1.D3_PWM, Composant2.SQW
  N8: Composant1.D2, Couvercle.COM
  N9: Raspberry_Pi_B_rev1.3V3, Composant3.VCCB
  N10: Raspberry_Pi_B_rev1.5V, U4.2
  N11: Raspberry_Pi_B_rev1.GIPO_0, Composant3.B1
  N12: Raspberry_Pi_B_rev1.GIPO_1, Composant3.B2
  N13: Raspberry_Pi_B_rev1.GPIO_11, Composant3.B3
  N14: U4.1, Q1.C

custom parts:
  Adafruit DS3231: The datasheet for the DS3231 explains that this part is an "Extremely Accurate I²C-Integrated RTC/TCXO/Crystal". And, hey, it does exactly what it says on the tin! This Real Time Clock (RTC) is the most precise you can get in a small, low power package. Most RTCs use an external 32kHz timing crystal that is used to keep time with low current draw. And that's all well and good, but those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
  TXB0108 8-channel Bi-directional Logic Level Converter: Because the Arduino (and Basic Stamp) are 5V devices, and most modern sensors, displays, flash cards and modes are 3.3V-only, many makers find that they need to perform level shifting/conversion to protect the 3.3V device from 5V. Although one can use resistors to make a divider, for high speed transfers, the resistors can add a lot of slew and cause havoc that is tough to debug. For that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
